// Logisim project LALU.circ as structural Verilog: 2 circuits, main circuit main
module main (
  input  [7:0] in_1,
  input  cin,
  input  select,
  input  store,
  input  reset,
  input  resetmem,
  output [15:0] out_7
);

  wire add_sub, and_1_out, button_1_out, clk, dcjump, decoder_1_add, decoder_1_jumpa, decoder_1_ld,
       decoder_1_loada, decoder_1_nop, decoder_1_storea, decoder_1_stre, decoder_1_sub, decoder_1_xchg,
       djump, enable, jumpA, jumpneg, ld, loadA, nand_1_out, nop, not_1_out, not_2_out, or_1_out, or_3_out,
       register_4_q, storeA, str, sub, xchg;
  wire [3:0] decoder_1_address, multiplexer_3_out, register_8_q;
  wire [4:0] counter_1_q, jumpaddr, multiplexer_1_out, register_1_q, register_2_q;
  wire [7:0] bit_extender_1_out, controlled_buffer_1_out, register_3_q;
  wire [14:0] sub_add_1_result;
  wire [15:0] Areg, Breg, multiplexer_2_out, multiplexer_4_out, multiplexer_5_out, multiplexer_6_out,
       multiplexer_7_out;

  and and_1 (and_1_out, dcjump, jumpneg);
  or or_1 (or_1_out, and_1_out, jumpA, djump);
  not not_1 (not_1_out, or_1_out);
  Multiplexer #(.width(5), .enable("false")) multiplexer_1 (
    .in0(jumpaddr), .in1(Areg[4:0]), .out(multiplexer_1_out), .sel(jumpA));
  assign controlled_buffer_1_out = store ? in_1 : 8'bz;  // Controlled_Buffer controlled_buffer_1
  Counter #(.width(5), .max('h1f)) counter_1 (
    .load(or_1_out), .D(multiplexer_1_out), .count(not_1_out), .Q(counter_1_q), .clk(clk), .clr(reset));  // open: carry
  Register #(.width(5)) register_1 (.D(register_2_q), .en(1'b1), .Q(register_1_q), .clk(clk), .clr(reset));
  Register #(.width(5)) register_2 (.D(counter_1_q), .en(1'b1), .Q(register_2_q), .clk(clk), .clr(reset));
  assign bit_extender_1_out = {{3{1'b0}}, register_1_q};  // Bit_Extender bit_extender_1
  RAM #(.addrWidth(5), .bus("asynch")) ram_1 (
    .addr(counter_1_q), .data(controlled_buffer_1_out), .sel(enable), .ld(not_2_out), .clr(resetmem));
  not not_2 (not_2_out, store);
  Clock u_clk (.out(clk));
  T_Flip_Flop t_ff_1 (.clk(button_1_out), .T(button_1_out), .Qn(enable));  // open: Q, preset, reset, en
  Button button_1 (.out(button_1_out));
  Hex_Digit_Display hex_digit_display_1 (.value(bit_extender_1_out[3:0]));  // open: dp
  Hex_Digit_Display hex_digit_display_2 (.value(bit_extender_1_out[7:4]));  // open: dp
  Register register_3 (.D(controlled_buffer_1_out), .Q(register_3_q), .clk(clk), .clr(reset));  // open: en
  decoder decoder_1 (
    .instr(register_3_q), .add(decoder_1_add), .sub(decoder_1_sub), .ld(decoder_1_ld), .xchg(decoder_1_xchg),
    .address(decoder_1_address), .stre(decoder_1_stre), .jumpA(decoder_1_jumpa), .address2(jumpaddr),
    .djump(djump), .jumpneg(dcjump), .nop(decoder_1_nop), .loadA(decoder_1_loada), .storeA(decoder_1_storea));
  Hex_Digit_Display hex_digit_display_3 (.value(Areg[15:12]));  // open: dp
  Register #(.width(1)) register_4 (.D(decoder_1_add), .en(1'b1), .Q(register_4_q), .clk(clk), .clr(reset));
  or or_2 (add_sub, register_4_q, sub);
  Register #(.width(1)) register_5 (.D(decoder_1_sub), .en(1'b1), .Q(sub), .clk(clk), .clr(reset));
  Register #(.width(1)) register_6 (.D(decoder_1_ld), .en(1'b1), .Q(ld), .clk(clk), .clr(reset));
  Register #(.width(1)) register_7 (.D(decoder_1_xchg), .en(1'b1), .Q(xchg), .clk(clk), .clr(reset));
  Register #(.width(4)) register_8 (.D(decoder_1_address), .en(1'b1), .Q(register_8_q), .clk(clk), .clr(reset));
  Register #(.width(1)) register_9 (.D(decoder_1_stre), .Q(str), .clk(clk), .clr(reset));  // open: en
  Register #(.width(1)) register_10 (.D(djump), .en(1'b1), .clk(clk), .clr(reset));  // open: Q
  Register #(.width(1)) register_11 (.D(dcjump), .en(1'b1), .clk(clk), .clr(reset));  // open: Q
  Register #(.width(5)) register_12 (.D(jumpaddr), .en(1'b1), .clk(clk), .clr(reset));  // open: Q
  Register #(.width(1)) register_13 (.D(decoder_1_loada), .en(1'b1), .Q(loadA), .clk(clk), .clr(reset));
  Register #(.width(1)) register_14 (.D(decoder_1_nop), .en(1'b1), .Q(nop), .clk(clk), .clr(reset));
  Register #(.width(1)) register_15 (.D(decoder_1_storea), .en(1'b1), .Q(storeA), .clk(clk), .clr(reset));
  Register #(.width(1)) register_16 (.D(decoder_1_jumpa), .en(1'b1), .Q(jumpA), .clk(clk), .clr(reset));
  Hex_Digit_Display hex_digit_display_4 (.value(Areg[11:8]));  // open: dp
  Multiplexer #(.width(16), .enable("false")) multiplexer_2 (
    .in0(Areg), .in1(Breg), .out(multiplexer_2_out), .sel(storeA));
  Hex_Digit_Display hex_digit_display_5 (.value(Areg[7:4]));  // open: dp
  Hex_Digit_Display hex_digit_display_6 (.value(Areg[3:0]));  // open: dp
  assign out_7 = str ? multiplexer_2_out : 16'bz;  // Controlled_Buffer controlled_buffer_2
  Multiplexer #(.width(4), .enable("false")) multiplexer_3 (
    .in0(register_8_q), .in1(Areg[3:0]), .out(multiplexer_3_out), .sel(loadA));
  Hex_Digit_Display hex_digit_display_7 (.value(Breg[15:12]));  // open: dp
  sub_add sub_add_1 (
    .cin(cin), .sub(sub), .a(Areg), .b(Breg), .result({jumpneg, sub_add_1_result}), .select(select));  // open: cout, overflow
  nand nand_1 (nand_1_out, enable, str);
  Hex_Digit_Display hex_digit_display_8 (.value(Breg[11:8]));  // open: dp
  Hex_Digit_Display hex_digit_display_9 (.value(Breg[7:4]));  // open: dp
  Multiplexer #(.width(16), .enable("false")) multiplexer_4 (
    .in0(Areg), .in1({jumpneg, sub_add_1_result}), .out(multiplexer_4_out), .sel(add_sub));
  RAM #(.addrWidth(4), .dataWidth(16)) ram_2 (
    .addr(multiplexer_3_out), .data(out_7), .sel(enable), .clk(clk), .ld(nand_1_out), .clr(resetmem));
  Hex_Digit_Display hex_digit_display_10 (.value(Breg[3:0]));  // open: dp
  or or_3 (or_3_out, ld, loadA);
  Multiplexer #(.width(16), .enable("false")) multiplexer_5 (
    .in0(multiplexer_4_out), .in1(out_7), .out(multiplexer_5_out), .sel(or_3_out));
  Multiplexer #(.width(16), .enable("false")) multiplexer_6 (
    .in0(multiplexer_5_out), .in1(Breg), .out(multiplexer_6_out), .sel(xchg));
  Multiplexer #(.width(16), .enable("false")) multiplexer_7 (
    .in0(Breg), .in1(Areg), .out(multiplexer_7_out), .sel(xchg));
  Register #(.width(16)) register_17 (.D(multiplexer_6_out), .en(1'b1), .Q(Areg), .clk(clk), .clr(reset));
  Register #(.width(16)) register_18 (.D(multiplexer_7_out), .en(1'b1), .Q(Breg), .clk(clk), .clr(reset));

  // Other names for the same wires on the sheet: memory[15:0] = out_7

  // Notes on the sheet:
  //   Instruction Memory
  //   POWER
  //   data memory
endmodule

module decoder (
  input  [7:0] instr,
  output add,
  output sub,
  output ld,
  output xchg,
  output stre,
  output djump,
  output jumpneg,
  output loadA,
  output nop,
  output storeA,
  output jumpA,
  output [3:0] address,
  output [4:0] address2
);

  wire nor_2_out, nor_3_out, nor_4_out, nor_5_out;

  nor nor_1 (add, instr[0], instr[1], instr[2], instr[3]);
  and and_1 (sub, instr[0], nor_2_out);
  nor nor_2 (nor_2_out, instr[1], instr[2], instr[3]);
  and and_2 (ld, instr[1], nor_3_out);
  nor nor_3 (nor_3_out, instr[0], instr[2], instr[3]);
  and and_3 (xchg, instr[0], instr[1], nor_4_out);
  nor nor_4 (nor_4_out, instr[2], instr[3]);
  and and_4 (stre, instr[2], nor_5_out);
  nor nor_5 (nor_5_out, instr[0], instr[1], instr[3]);
  and and_5 (djump, instr[0], ~instr[1], instr[2]);  // AND_Gate
  and and_6 (jumpneg, ~instr[0], instr[1], instr[2]);  // AND_Gate
  and and_7 (loadA, instr[0], instr[1], instr[2], ~instr[3]);  // AND_Gate
  and and_8 (nop, ~instr[0], ~instr[1], ~instr[2], instr[3]);  // AND_Gate
  and and_9 (storeA, instr[0], ~instr[1], ~instr[2], instr[3]);  // AND_Gate
  and and_10 (jumpA, instr[0], instr[1], instr[2], instr[3]);

  assign address = instr[7:4];
  assign address2 = instr[7:3];
endmodule
