// Logisim project Lookahead Carry Unit.circ as structural Verilog: 11 circuits, main circuit 4-bit LCU adder
module _1_bit_adder_w_P_G (
  input  a,
  input  b,
  input  carryin,
  output Sum,
  output G_Half_Carry,
  output P_Half_Sum
);

  wire nand_1_out, nand_2_out, nand_3_out, nand_4_out, nand_6_out, not_1_out, not_2_out, not_3_out, not_4_out;

  not not_1 (not_1_out, a);
  not not_2 (not_2_out, b);
  nand nand_1 (nand_1_out, b, not_1_out);
  nand nand_2 (nand_2_out, a, not_2_out);
  nand nand_3 (nand_3_out, nand_1_out, nand_2_out);
  and and_1 (G_Half_Carry, a, b);
  or or_1 (P_Half_Sum, a, b);
  not not_3 (not_3_out, carryin);
  not not_4 (not_4_out, nand_3_out);
  nand nand_4 (nand_4_out, nand_3_out, not_3_out);
  nand nand_5 (Sum, nand_4_out, nand_6_out);
  nand nand_6 (nand_6_out, carryin, not_4_out);
endmodule

module _4_bit_LCU_adder (
  input  [3:0] in_1,
  input  [3:0] in_2,
  input  cin,
  output [3:0] out_4,
  output cout
);

  wire and_1_out, and_2_out, and_3_out, and_4_out, and_5_out, and_6_out, and_7_out, and_8_out, and_9_out,
       and_10_out, n1_bit_adder_w_p_g_1_g_half_carry, n1_bit_adder_w_p_g_1_p_half_sum,
       n1_bit_adder_w_p_g_2_g_half_carry, n1_bit_adder_w_p_g_2_p_half_sum, n1_bit_adder_w_p_g_3_g_half_carry,
       n1_bit_adder_w_p_g_3_p_half_sum, n1_bit_adder_w_p_g_4_g_half_carry, n1_bit_adder_w_p_g_4_p_half_sum,
       or_1_out, or_2_out, or_3_out;

  _1_bit_adder_w_P_G u_1_bit_adder_w_p_g_1 (
    .a(in_2[0]), .b(in_1[0]), .carryin(cin), .P_Half_Sum(n1_bit_adder_w_p_g_1_p_half_sum), .Sum(out_4[0]),
    .G_Half_Carry(n1_bit_adder_w_p_g_1_g_half_carry));
  and and_1 (and_1_out, cin, n1_bit_adder_w_p_g_1_p_half_sum);
  or or_1 (or_1_out, and_1_out, n1_bit_adder_w_p_g_1_g_half_carry);
  _1_bit_adder_w_P_G u_1_bit_adder_w_p_g_2 (
    .a(in_2[1]), .b(in_1[1]), .carryin(or_1_out), .P_Half_Sum(n1_bit_adder_w_p_g_2_p_half_sum),
    .Sum(out_4[1]), .G_Half_Carry(n1_bit_adder_w_p_g_2_g_half_carry));
  and and_2 (and_2_out, cin, n1_bit_adder_w_p_g_1_p_half_sum, n1_bit_adder_w_p_g_2_p_half_sum);
  and and_3 (and_3_out, n1_bit_adder_w_p_g_1_g_half_carry, n1_bit_adder_w_p_g_2_p_half_sum);
  or or_2 (or_2_out, and_2_out, and_3_out, n1_bit_adder_w_p_g_2_g_half_carry);
  _1_bit_adder_w_P_G u_1_bit_adder_w_p_g_3 (
    .a(in_2[2]), .b(in_1[2]), .carryin(or_2_out), .P_Half_Sum(n1_bit_adder_w_p_g_3_p_half_sum),
    .Sum(out_4[2]), .G_Half_Carry(n1_bit_adder_w_p_g_3_g_half_carry));
  and and_4 (and_4_out, cin, n1_bit_adder_w_p_g_1_p_half_sum, n1_bit_adder_w_p_g_2_p_half_sum, n1_bit_adder_w_p_g_3_p_half_sum);
  and and_5 (and_5_out, n1_bit_adder_w_p_g_1_g_half_carry, n1_bit_adder_w_p_g_2_p_half_sum, n1_bit_adder_w_p_g_3_p_half_sum);
  or or_3 (or_3_out, and_4_out, and_5_out, and_6_out, n1_bit_adder_w_p_g_3_g_half_carry);
  _1_bit_adder_w_P_G u_1_bit_adder_w_p_g_4 (
    .a(in_2[3]), .b(in_1[3]), .carryin(or_3_out), .P_Half_Sum(n1_bit_adder_w_p_g_4_p_half_sum),
    .Sum(out_4[3]), .G_Half_Carry(n1_bit_adder_w_p_g_4_g_half_carry));
  and and_6 (and_6_out, n1_bit_adder_w_p_g_2_g_half_carry, n1_bit_adder_w_p_g_3_p_half_sum);
  and and_7 (and_7_out, cin, n1_bit_adder_w_p_g_1_p_half_sum, n1_bit_adder_w_p_g_2_p_half_sum, n1_bit_adder_w_p_g_3_p_half_sum, n1_bit_adder_w_p_g_4_p_half_sum);
  and and_8 (and_8_out, n1_bit_adder_w_p_g_1_g_half_carry, n1_bit_adder_w_p_g_1_p_half_sum, n1_bit_adder_w_p_g_2_p_half_sum, n1_bit_adder_w_p_g_4_p_half_sum);
  and and_9 (and_9_out, n1_bit_adder_w_p_g_2_g_half_carry, n1_bit_adder_w_p_g_3_p_half_sum, n1_bit_adder_w_p_g_4_p_half_sum);
  or or_4 (cout, and_7_out, and_8_out, and_9_out, and_10_out, n1_bit_adder_w_p_g_4_g_half_carry);
  and and_10 (and_10_out, n1_bit_adder_w_p_g_3_g_half_carry, n1_bit_adder_w_p_g_4_p_half_sum);
endmodule

module _4_bit_LCU_adder_w__P_G_out (
  input  [3:0] in_1,
  input  [3:0] in_2,
  input  cin,
  output Gout,
  output Pout,
  output [3:0] out_6
);

  wire and_1_out, and_2_out, and_3_out, and_4_out, and_5_out, and_6_out, n1_bit_adder_w_p_g_2_g_half_carry,
       n1_bit_adder_w_p_g_2_p_half_sum, n1_bit_adder_w_p_g_3_g_half_carry, n1_bit_adder_w_p_g_3_p_half_sum,
       or_1_out, or_2_out, or_3_out;

  _1_bit_adder_w_P_G u_1_bit_adder_w_p_g_1 (
    .a(in_2[0]), .b(in_1[0]), .carryin(cin), .P_Half_Sum(Pout), .Sum(out_6[0]), .G_Half_Carry(Gout));
  and and_1 (and_1_out, cin, Pout);
  or or_1 (or_1_out, and_1_out, Gout);
  _1_bit_adder_w_P_G u_1_bit_adder_w_p_g_2 (
    .a(in_2[1]), .b(in_1[1]), .carryin(or_1_out), .P_Half_Sum(n1_bit_adder_w_p_g_2_p_half_sum),
    .Sum(out_6[1]), .G_Half_Carry(n1_bit_adder_w_p_g_2_g_half_carry));
  and and_2 (and_2_out, Gout, n1_bit_adder_w_p_g_2_p_half_sum);
  and and_3 (and_3_out, cin, Pout, n1_bit_adder_w_p_g_2_p_half_sum);
  or or_2 (or_2_out, and_3_out, and_2_out, n1_bit_adder_w_p_g_2_g_half_carry);
  _1_bit_adder_w_P_G u_1_bit_adder_w_p_g_3 (
    .a(in_2[2]), .b(in_1[2]), .carryin(or_2_out), .P_Half_Sum(n1_bit_adder_w_p_g_3_p_half_sum),
    .Sum(out_6[2]), .G_Half_Carry(n1_bit_adder_w_p_g_3_g_half_carry));
  and and_4 (and_4_out, cin, Pout, n1_bit_adder_w_p_g_2_p_half_sum, n1_bit_adder_w_p_g_3_p_half_sum);
  and and_5 (and_5_out, Gout, n1_bit_adder_w_p_g_2_p_half_sum, n1_bit_adder_w_p_g_3_p_half_sum);
  and and_6 (and_6_out, n1_bit_adder_w_p_g_2_g_half_carry, n1_bit_adder_w_p_g_3_p_half_sum);
  or or_3 (or_3_out, and_4_out, and_5_out, and_6_out, n1_bit_adder_w_p_g_3_g_half_carry);
  _1_bit_adder_w_P_G u_1_bit_adder_w_p_g_4 (
    .a(in_2[3]), .b(in_1[3]), .carryin(or_3_out), .Sum(out_6[3]));  // open: P_Half_Sum, G_Half_Carry
endmodule

module _16_bit_LCU_adder (
  input  [15:0] in_1,
  input  [15:0] in_2,
  input  cin,
  output [15:0] out_4,
  output cout
);

  wire and_1_out, and_2_out, and_3_out, and_4_out, and_5_out, and_6_out, and_7_out, and_8_out, and_9_out,
       and_10_out, n4_bit_lcu_adder_w_p_g_out_1_gout, n4_bit_lcu_adder_w_p_g_out_1_pout,
       n4_bit_lcu_adder_w_p_g_out_2_gout, n4_bit_lcu_adder_w_p_g_out_2_pout,
       n4_bit_lcu_adder_w_p_g_out_3_gout, n4_bit_lcu_adder_w_p_g_out_3_pout,
       n4_bit_lcu_adder_w_p_g_out_4_gout, n4_bit_lcu_adder_w_p_g_out_4_pout, or_1_out, or_2_out, or_3_out;

  _4_bit_LCU_adder_w__P_G_out u_4_bit_lcu_adder_w_p_g_out_1 (
    .in_1(in_2[3:0]), .in_2(in_1[3:0]), .cin(cin), .Gout(n4_bit_lcu_adder_w_p_g_out_1_gout),
    .Pout(n4_bit_lcu_adder_w_p_g_out_1_pout), .out_6(out_4[3:0]));
  and and_1 (and_1_out, cin, n4_bit_lcu_adder_w_p_g_out_1_pout);
  or or_1 (or_1_out, and_1_out, n4_bit_lcu_adder_w_p_g_out_1_gout);
  _4_bit_LCU_adder_w__P_G_out u_4_bit_lcu_adder_w_p_g_out_2 (
    .in_1(in_2[7:4]), .in_2(in_1[7:4]), .cin(or_1_out), .Gout(n4_bit_lcu_adder_w_p_g_out_2_gout),
    .Pout(n4_bit_lcu_adder_w_p_g_out_2_pout), .out_6(out_4[7:4]));
  and and_2 (and_2_out, cin, n4_bit_lcu_adder_w_p_g_out_1_pout, n4_bit_lcu_adder_w_p_g_out_2_pout);
  and and_3 (and_3_out, n4_bit_lcu_adder_w_p_g_out_1_gout, n4_bit_lcu_adder_w_p_g_out_2_pout);
  or or_2 (or_2_out, and_2_out, and_3_out, n4_bit_lcu_adder_w_p_g_out_2_gout);
  _4_bit_LCU_adder_w__P_G_out u_4_bit_lcu_adder_w_p_g_out_3 (
    .in_1(in_2[11:8]), .in_2(in_1[11:8]), .cin(or_2_out), .Gout(n4_bit_lcu_adder_w_p_g_out_3_gout),
    .Pout(n4_bit_lcu_adder_w_p_g_out_3_pout), .out_6(out_4[11:8]));
  and and_4 (and_4_out, cin, n4_bit_lcu_adder_w_p_g_out_1_pout, n4_bit_lcu_adder_w_p_g_out_2_pout, n4_bit_lcu_adder_w_p_g_out_3_pout);
  and and_5 (and_5_out, n4_bit_lcu_adder_w_p_g_out_2_gout, n4_bit_lcu_adder_w_p_g_out_3_pout);
  and and_6 (and_6_out, n4_bit_lcu_adder_w_p_g_out_1_gout, n4_bit_lcu_adder_w_p_g_out_2_pout, n4_bit_lcu_adder_w_p_g_out_3_pout);
  or or_3 (or_3_out, and_4_out, and_6_out, and_5_out, n4_bit_lcu_adder_w_p_g_out_3_gout);
  _4_bit_LCU_adder_w__P_G_out u_4_bit_lcu_adder_w_p_g_out_4 (
    .in_1(in_2[15:12]), .in_2(in_1[15:12]), .cin(or_3_out), .Gout(n4_bit_lcu_adder_w_p_g_out_4_gout),
    .Pout(n4_bit_lcu_adder_w_p_g_out_4_pout), .out_6(out_4[15:12]));
  and and_7 (and_7_out, n4_bit_lcu_adder_w_p_g_out_1_gout, n4_bit_lcu_adder_w_p_g_out_1_pout, n4_bit_lcu_adder_w_p_g_out_2_pout, n4_bit_lcu_adder_w_p_g_out_4_pout);
  and and_8 (and_8_out, cin, n4_bit_lcu_adder_w_p_g_out_1_pout, n4_bit_lcu_adder_w_p_g_out_2_pout, n4_bit_lcu_adder_w_p_g_out_3_pout, n4_bit_lcu_adder_w_p_g_out_4_pout);
  and and_9 (and_9_out, n4_bit_lcu_adder_w_p_g_out_2_gout, n4_bit_lcu_adder_w_p_g_out_3_pout, n4_bit_lcu_adder_w_p_g_out_4_pout);
  or or_4 (cout, and_8_out, and_7_out, and_9_out, and_10_out, n4_bit_lcu_adder_w_p_g_out_4_gout);
  and and_10 (and_10_out, n4_bit_lcu_adder_w_p_g_out_3_gout, n4_bit_lcu_adder_w_p_g_out_4_pout);
endmodule

module _4_bit_LCU_for_analysis (
  input  b3,
  input  b2,
  input  b1,
  input  b0,
  input  a3,
  input  a2,
  input  a1,
  input  a0,
  input  cin,
  output out_10,
  output out_11,
  output out_12,
  output out_13,
  output overflow
);

  wire and_1_out, and_2_out, and_3_out, nand_1_out, nand_2_out, nand_3_out, nand_4_out, nand_5_out,
       nand_6_out, nand_7_out, nand_9_out, nand_10_out, nand_11_out, nand_12_out, nand_13_out, nand_15_out,
       nand_16_out, nand_17_out, nand_18_out, nand_19_out, nand_20_out, nand_21_out, nand_22_out,
       nand_23_out, nand_24_out, nand_25_out, nand_27_out, nand_28_out, nand_29_out, nand_30_out,
       nand_31_out, nand_32_out, nand_33_out, nand_34_out, nand_36_out, nand_37_out, nand_38_out,
       nand_39_out, not_1_out, not_2_out, not_3_out, not_5_out, not_6_out, not_7_out, not_8_out, not_9_out,
       not_10_out, not_11_out, not_12_out, not_13_out, not_14_out, not_15_out, not_16_out, not_17_out,
       not_18_out, not_19_out, or_1_out, or_2_out, or_3_out, or_4_out, xor_1_out, xor_2_out, xor_3_out,
       xor_4_out;

  or or_1 (or_1_out, xor_4_out, a0);
  xor xor_1 (xor_1_out, b3, cin);
  xor xor_2 (xor_2_out, b2, cin);
  xor xor_3 (xor_3_out, b1, cin);
  xor xor_4 (xor_4_out, b0, cin);
  nand nand_1 (nand_1_out, xor_4_out, not_1_out);
  not not_1 (not_1_out, a0);
  not not_2 (not_2_out, xor_4_out);
  and and_1 (and_1_out, xor_4_out, a0);
  not not_3 (not_3_out, cin);
  nand nand_2 (nand_2_out, cin, or_1_out);
  nand nand_3 (nand_3_out, nand_2_out, not_5_out);
  nand nand_4 (nand_4_out, nand_1_out, nand_5_out);
  nand nand_5 (nand_5_out, a0, not_2_out);
  // NOT_Gate not_4 has open pins: in=nand_4_out, out=open
  nand nand_6 (nand_6_out, nand_4_out, cin);
  nand nand_7 (nand_7_out, not_3_out, nand_4_out);
  nand nand_8 (out_13, nand_7_out, nand_6_out);
  not not_5 (not_5_out, and_1_out);
  not not_6 (not_6_out, a1);
  or or_2 (or_2_out, xor_3_out, a1);
  and and_2 (and_2_out, xor_3_out, a1);
  nand nand_9 (nand_9_out, cin, or_1_out, or_2_out);
  nand nand_10 (nand_10_out, xor_3_out, not_6_out);
  nand nand_11 (nand_11_out, a1, not_7_out);
  not not_7 (not_7_out, xor_3_out);
  not not_8 (not_8_out, nand_17_out);
  not not_9 (not_9_out, nand_3_out);
  nand nand_12 (nand_12_out, not_8_out, nand_3_out);
  nand nand_13 (nand_13_out, not_9_out, nand_17_out);
  nand nand_14 (out_12, nand_13_out, nand_12_out);
  not not_10 (not_10_out, and_2_out);
  nand nand_15 (nand_15_out, and_1_out, or_2_out);
  nand nand_16 (nand_16_out, nand_9_out, nand_15_out, not_10_out);
  nand nand_17 (nand_17_out, nand_10_out, nand_11_out);
  or or_3 (or_3_out, xor_2_out, a2);
  nand nand_18 (nand_18_out, cin, or_1_out, or_2_out, or_3_out);
  nand nand_19 (nand_19_out, xor_2_out, not_11_out);
  not not_11 (not_11_out, a2);
  not not_12 (not_12_out, xor_2_out);
  not not_13 (not_13_out, nand_16_out);
  and and_3 (and_3_out, xor_2_out, a2);
  nand nand_20 (nand_20_out, and_1_out, or_2_out, or_3_out);
  nand nand_21 (nand_21_out, nand_18_out, nand_20_out, nand_27_out, not_15_out);
  nand nand_22 (nand_22_out, nand_19_out, nand_23_out);
  nand nand_23 (nand_23_out, a2, not_12_out);
  not not_14 (not_14_out, nand_22_out);
  nand nand_24 (nand_24_out, not_13_out, nand_22_out);
  nand nand_25 (nand_25_out, not_14_out, nand_16_out);
  nand nand_26 (out_11, nand_24_out, nand_25_out);
  nand nand_27 (nand_27_out, and_2_out, or_3_out);
  not not_15 (not_15_out, and_3_out);
  not not_16 (not_16_out, a3);
  or or_4 (or_4_out, xor_1_out, a3);
  nand nand_28 (nand_28_out, xor_1_out, a3);
  nand nand_29 (nand_29_out, cin, or_1_out, or_2_out, or_3_out, or_4_out);
  nand nand_30 (nand_30_out, and_1_out, or_1_out, or_2_out, or_4_out);
  nand nand_31 (nand_31_out, xor_1_out, not_16_out);
  nand nand_32 (nand_32_out, a3, not_17_out);
  not not_17 (not_17_out, xor_1_out);
  not not_18 (not_18_out, nand_38_out);
  not not_19 (not_19_out, nand_21_out);
  nand nand_33 (nand_33_out, not_18_out, nand_21_out);
  nand nand_34 (nand_34_out, not_19_out, nand_38_out);
  nand nand_35 (out_10, nand_34_out, nand_33_out);
  nand nand_36 (nand_36_out, and_2_out, or_3_out, or_4_out);
  nand nand_37 (nand_37_out, nand_29_out, nand_30_out, nand_36_out, nand_39_out, nand_28_out);
  nand nand_38 (nand_38_out, nand_31_out, nand_32_out);
  nand nand_39 (nand_39_out, and_3_out, or_4_out);
  xor xor_5 (overflow, nand_37_out, nand_21_out);

  // Notes on the sheet:
  //   g rails
  //   p rails
endmodule

module _4_bit_LCU_for_analysis_auto_generated_NAND_only (
  input  a,
  input  b,
  input  c,
  input  d,
  input  e,
  input  f,
  input  g,
  input  h,
  input  cin,
  output x,
  output y,
  output z,
  output u,
  output cout
);

  wire nand_1_out, nand_2_out, nand_3_out, nand_4_out, nand_5_out, nand_6_out, nand_7_out, nand_8_out,
       nand_9_out, nand_10_out, nand_11_out, nand_12_out, nand_13_out, nand_14_out, nand_15_out, nand_16_out,
       nand_17_out, nand_18_out, nand_19_out, nand_20_out, nand_21_out, nand_22_out, nand_23_out,
       nand_24_out, nand_25_out, nand_26_out, nand_27_out, nand_28_out, nand_29_out, nand_30_out,
       nand_31_out, nand_32_out, nand_33_out, nand_34_out, nand_35_out, nand_36_out, nand_37_out,
       nand_38_out, nand_39_out, nand_40_out, nand_41_out, nand_42_out, nand_43_out, nand_44_out,
       nand_45_out, nand_46_out, nand_47_out, nand_48_out, nand_49_out, nand_50_out, nand_51_out,
       nand_52_out, nand_53_out, nand_54_out, nand_55_out, nand_56_out, nand_57_out, nand_58_out,
       nand_59_out, nand_60_out, nand_61_out, nand_62_out, nand_63_out, nand_64_out, nand_65_out,
       nand_66_out, nand_67_out, nand_68_out, nand_69_out, nand_70_out, nand_71_out, nand_72_out,
       nand_73_out, nand_74_out, nand_75_out, nand_76_out, nand_77_out, nand_78_out, nand_79_out,
       nand_80_out, nand_81_out, nand_82_out, nand_83_out, nand_84_out, nand_85_out, nand_86_out,
       nand_87_out, nand_88_out, nand_89_out, nand_90_out, nand_91_out, nand_92_out, nand_93_out,
       nand_94_out, nand_95_out, nand_96_out, nand_97_out, nand_98_out, nand_99_out, nand_100_out,
       nand_101_out, nand_102_out, nand_103_out, nand_104_out, nand_105_out, nand_106_out, nand_107_out,
       nand_108_out, nand_109_out, nand_110_out, nand_111_out, nand_112_out, nand_113_out, nand_114_out,
       nand_115_out, nand_116_out, nand_117_out, nand_118_out, nand_119_out, nand_120_out, nand_121_out,
       nand_122_out, nand_123_out, nand_124_out, nand_125_out, nand_126_out, nand_127_out, nand_128_out,
       nand_129_out, nand_130_out, nand_131_out, nand_132_out, nand_133_out, nand_134_out, nand_135_out,
       nand_136_out, nand_137_out, nand_138_out, nand_139_out, nand_140_out, nand_141_out, nand_142_out,
       nand_143_out, nand_144_out, nand_145_out, nand_146_out, nand_147_out, nand_148_out, nand_149_out,
       nand_150_out, nand_151_out, nand_152_out, nand_153_out, nand_154_out, nand_155_out, nand_156_out,
       nand_157_out, nand_158_out, nand_159_out, nand_160_out, nand_161_out, nand_162_out, nand_163_out,
       nand_164_out, nand_165_out, nand_166_out, nand_167_out, nand_168_out, nand_169_out, nand_170_out,
       nand_171_out, nand_172_out, nand_173_out, nand_174_out, nand_176_out, nand_177_out, nand_178_out,
       nand_179_out, nand_180_out, nand_181_out, nand_182_out, nand_183_out, nand_184_out, nand_185_out,
       nand_186_out, nand_187_out, nand_188_out, nand_189_out, nand_190_out, nand_191_out, nand_192_out,
       nand_193_out, nand_194_out, nand_195_out, nand_196_out, nand_198_out, nand_199_out, nand_200_out,
       nand_201_out, nand_202_out, nand_203_out, nand_204_out, nand_205_out, nand_206_out, nand_207_out,
       nand_208_out, nand_209_out, nand_210_out, nand_211_out, nand_212_out, nand_213_out, nand_214_out,
       nand_215_out, nand_216_out, nand_217_out, nand_218_out, nand_219_out, nand_220_out, nand_221_out,
       nand_222_out, nand_223_out, nand_224_out, nand_225_out, nand_226_out, nand_227_out, nand_228_out,
       nand_229_out, nand_230_out, nand_231_out, nand_232_out, nand_233_out, nand_234_out, nand_235_out,
       nand_236_out, nand_237_out, nand_238_out, nand_239_out, nand_242_out, nand_243_out;

  nand nand_1 (nand_1_out, d, d);
  nand nand_2 (nand_2_out, h, h);
  nand nand_3 (nand_3_out, c, c);
  nand nand_4 (nand_4_out, g, g);
  nand nand_5 (nand_5_out, b, b);
  nand nand_6 (nand_6_out, f, f);
  nand nand_7 (nand_7_out, c, c);
  nand nand_8 (nand_8_out, g, g);
  nand nand_9 (nand_9_out, b, b);
  nand nand_10 (nand_10_out, f, f);
  nand nand_11 (nand_11_out, d, d);
  nand nand_12 (nand_12_out, h, h);
  nand nand_13 (nand_13_out, d, d);
  nand nand_14 (nand_14_out, h, h);
  nand nand_15 (nand_15_out, h, h);
  nand nand_16 (nand_16_out, d, d);
  nand nand_17 (nand_17_out, d, d);
  nand nand_18 (nand_18_out, h, h);
  nand nand_19 (nand_19_out, nand_1_out, nand_2_out);
  nand nand_20 (nand_20_out, nand_3_out, nand_4_out);
  nand nand_21 (nand_21_out, nand_5_out, nand_6_out);
  nand nand_22 (nand_22_out, nand_7_out, nand_8_out);
  nand nand_23 (nand_23_out, nand_9_out, nand_10_out);
  nand nand_24 (nand_24_out, d, d);
  nand nand_25 (nand_25_out, h, h);
  nand nand_26 (nand_26_out, c, c);
  nand nand_27 (nand_27_out, g, g);
  nand nand_28 (nand_28_out, b, b);
  nand nand_29 (nand_29_out, f, f);
  nand nand_30 (nand_30_out, c, c);
  nand nand_31 (nand_31_out, g, g);
  nand nand_32 (nand_32_out, b, b);
  nand nand_33 (nand_33_out, f, f);
  nand nand_34 (nand_34_out, nand_11_out, nand_12_out);
  nand nand_35 (nand_35_out, d, d);
  nand nand_36 (nand_36_out, h, h);
  nand nand_37 (nand_37_out, nand_13_out, nand_14_out);
  nand nand_38 (nand_38_out, g, g);
  nand nand_39 (nand_39_out, c, c);
  nand nand_40 (nand_40_out, d, d);
  nand nand_41 (nand_41_out, h, h);
  nand nand_42 (nand_42_out, h, h);
  nand nand_43 (nand_43_out, d, d);
  nand nand_44 (nand_44_out, d, nand_15_out);
  nand nand_45 (nand_45_out, h, nand_16_out);
  nand nand_46 (nand_46_out, nand_17_out, nand_18_out);
  nand nand_47 (nand_47_out, cin, nand_19_out);
  nand nand_48 (nand_48_out, nand_20_out, nand_21_out);
  nand nand_49 (nand_49_out, d, h);
  nand nand_50 (nand_50_out, nand_22_out, nand_23_out);
  nand nand_51 (nand_51_out, c, g);
  nand nand_52 (nand_52_out, b, b);
  nand nand_53 (nand_53_out, f, f);
  nand nand_54 (nand_54_out, nand_24_out, nand_25_out);
  nand nand_55 (nand_55_out, nand_26_out, nand_27_out);
  nand nand_56 (nand_56_out, nand_28_out, nand_29_out);
  nand nand_57 (nand_57_out, nand_30_out, nand_31_out);
  nand nand_58 (nand_58_out, nand_32_out, nand_33_out);
  nand nand_59 (nand_59_out, cin, nand_34_out);
  nand nand_60 (nand_60_out, c, c);
  nand nand_61 (nand_61_out, g, g);
  nand nand_62 (nand_62_out, d, h);
  nand nand_63 (nand_63_out, c, c);
  nand nand_64 (nand_64_out, g, g);
  nand nand_65 (nand_65_out, nand_35_out, nand_36_out);
  nand nand_66 (nand_66_out, cin, nand_37_out);
  nand nand_67 (nand_67_out, d, h);
  nand nand_68 (nand_68_out, g, g);
  nand nand_69 (nand_69_out, c, c);
  nand nand_70 (nand_70_out, c, nand_38_out);
  nand nand_71 (nand_71_out, g, nand_39_out);
  nand nand_72 (nand_72_out, nand_40_out, nand_41_out);
  nand nand_73 (nand_73_out, d, nand_42_out);
  nand nand_74 (nand_74_out, h, nand_43_out);
  nand nand_75 (nand_75_out, nand_44_out, nand_45_out);
  nand nand_76 (nand_76_out, cin, nand_46_out);
  nand nand_77 (nand_77_out, c, c);
  nand nand_78 (nand_78_out, g, g);
  nand nand_79 (nand_79_out, b, b);
  nand nand_80 (nand_80_out, f, f);
  nand nand_81 (nand_81_out, a, a);
  nand nand_82 (nand_82_out, e, e);
  nand nand_83 (nand_83_out, d, h);
  nand nand_84 (nand_84_out, d, d);
  nand nand_85 (nand_85_out, h, h);
  nand nand_86 (nand_86_out, c, c);
  nand nand_87 (nand_87_out, g, g);
  nand nand_88 (nand_88_out, a, a);
  nand nand_89 (nand_89_out, e, e);
  nand nand_90 (nand_90_out, nand_47_out, nand_47_out);
  nand nand_91 (nand_91_out, nand_48_out, nand_48_out);
  nand nand_92 (nand_92_out, nand_49_out, nand_49_out);
  nand nand_93 (nand_93_out, nand_50_out, nand_50_out);
  nand nand_94 (nand_94_out, nand_51_out, nand_51_out);
  nand nand_95 (nand_95_out, nand_52_out, nand_53_out);
  nand nand_96 (nand_96_out, cin, nand_54_out);
  nand nand_97 (nand_97_out, nand_55_out, nand_56_out);
  nand nand_98 (nand_98_out, d, h);
  nand nand_99 (nand_99_out, nand_57_out, nand_58_out);
  nand nand_100 (nand_100_out, c, g);
  nand nand_101 (nand_101_out, b, b);
  nand nand_102 (nand_102_out, f, f);
  nand nand_103 (nand_103_out, nand_59_out, nand_59_out);
  nand nand_104 (nand_104_out, nand_60_out, nand_61_out);
  nand nand_105 (nand_105_out, nand_62_out, nand_62_out);
  nand nand_106 (nand_106_out, nand_63_out, nand_64_out);
  nand nand_107 (nand_107_out, cin, nand_65_out);
  nand nand_108 (nand_108_out, c, c);
  nand nand_109 (nand_109_out, g, g);
  nand nand_110 (nand_110_out, d, h);
  nand nand_111 (nand_111_out, c, c);
  nand nand_112 (nand_112_out, g, g);
  nand nand_113 (nand_113_out, nand_66_out, nand_67_out);
  nand nand_114 (nand_114_out, c, nand_68_out);
  nand nand_115 (nand_115_out, g, nand_69_out);
  nand nand_116 (nand_116_out, nand_70_out, nand_71_out);
  nand nand_117 (nand_117_out, cin, nand_72_out);
  nand nand_118 (nand_118_out, d, h);
  nand nand_119 (nand_119_out, cin, cin);
  nand nand_120 (nand_120_out, nand_73_out, nand_74_out);
  nand nand_121 (nand_121_out, nand_75_out, nand_75_out);
  nand nand_122 (nand_122_out, nand_76_out, nand_76_out);
  nand nand_123 (nand_123_out, nand_77_out, nand_78_out);
  nand nand_124 (nand_124_out, nand_79_out, nand_80_out);
  nand nand_125 (nand_125_out, nand_81_out, nand_82_out);
  nand nand_126 (nand_126_out, nand_83_out, nand_83_out);
  nand nand_127 (nand_127_out, nand_84_out, nand_85_out);
  nand nand_128 (nand_128_out, nand_86_out, nand_87_out);
  nand nand_129 (nand_129_out, nand_88_out, nand_89_out);
  nand nand_130 (nand_130_out, nand_90_out, nand_91_out);
  nand nand_131 (nand_131_out, nand_92_out, nand_93_out);
  nand nand_132 (nand_132_out, nand_94_out, nand_95_out);
  nand nand_133 (nand_133_out, b, f);
  nand nand_134 (nand_134_out, nand_96_out, nand_96_out);
  nand nand_135 (nand_135_out, nand_97_out, nand_97_out);
  nand nand_136 (nand_136_out, nand_98_out, nand_98_out);
  nand nand_137 (nand_137_out, nand_99_out, nand_99_out);
  nand nand_138 (nand_138_out, nand_100_out, nand_100_out);
  nand nand_139 (nand_139_out, nand_101_out, nand_102_out);
  nand nand_140 (nand_140_out, nand_103_out, nand_104_out);
  nand nand_141 (nand_141_out, nand_105_out, nand_106_out);
  nand nand_142 (nand_142_out, nand_107_out, nand_107_out);
  nand nand_143 (nand_143_out, nand_108_out, nand_109_out);
  nand nand_144 (nand_144_out, nand_110_out, nand_110_out);
  nand nand_145 (nand_145_out, nand_111_out, nand_112_out);
  nand nand_146 (nand_146_out, nand_113_out, nand_113_out);
  nand nand_147 (nand_147_out, nand_114_out, nand_115_out);
  nand nand_148 (nand_148_out, nand_116_out, nand_116_out);
  nand nand_149 (nand_149_out, nand_117_out, nand_118_out);
  nand nand_150 (nand_150_out, nand_119_out, nand_120_out);
  nand nand_151 (nand_151_out, nand_121_out, cin);
  nand nand_152 (nand_152_out, nand_122_out, nand_123_out);
  nand nand_153 (nand_153_out, nand_124_out, nand_125_out);
  nand nand_154 (nand_154_out, nand_126_out, nand_127_out);
  nand nand_155 (nand_155_out, nand_128_out, nand_129_out);
  nand nand_156 (nand_156_out, b, b);
  nand nand_157 (nand_157_out, f, f);
  nand nand_158 (nand_158_out, a, a);
  nand nand_159 (nand_159_out, e, e);
  nand nand_160 (nand_160_out, nand_130_out, nand_131_out);
  nand nand_161 (nand_161_out, nand_132_out, nand_133_out);
  nand nand_162 (nand_162_out, e, e);
  nand nand_163 (nand_163_out, a, a);
  nand nand_164 (nand_164_out, nand_134_out, nand_135_out);
  nand nand_165 (nand_165_out, nand_136_out, nand_137_out);
  nand nand_166 (nand_166_out, nand_138_out, nand_139_out);
  nand nand_167 (nand_167_out, b, f);
  nand nand_168 (nand_168_out, nand_140_out, nand_141_out);
  nand nand_169 (nand_169_out, f, f);
  nand nand_170 (nand_170_out, b, b);
  nand nand_171 (nand_171_out, nand_142_out, nand_143_out);
  nand nand_172 (nand_172_out, nand_144_out, nand_145_out);
  nand nand_173 (nand_173_out, nand_146_out, nand_147_out);
  nand nand_174 (nand_174_out, nand_148_out, nand_149_out);
  nand nand_175 (u, nand_150_out, nand_151_out);
  nand nand_176 (nand_176_out, nand_152_out, nand_152_out);
  nand nand_177 (nand_177_out, nand_153_out, nand_153_out);
  nand nand_178 (nand_178_out, nand_154_out, nand_154_out);
  nand nand_179 (nand_179_out, nand_155_out, nand_155_out);
  nand nand_180 (nand_180_out, nand_156_out, nand_157_out);
  nand nand_181 (nand_181_out, nand_158_out, nand_159_out);
  nand nand_182 (nand_182_out, nand_160_out, nand_160_out);
  nand nand_183 (nand_183_out, nand_161_out, nand_161_out);
  nand nand_184 (nand_184_out, e, e);
  nand nand_185 (nand_185_out, a, a);
  nand nand_186 (nand_186_out, a, nand_162_out);
  nand nand_187 (nand_187_out, e, nand_163_out);
  nand nand_188 (nand_188_out, nand_164_out, nand_165_out);
  nand nand_189 (nand_189_out, nand_166_out, nand_167_out);
  nand nand_190 (nand_190_out, nand_168_out, nand_168_out);
  nand nand_191 (nand_191_out, c, g);
  nand nand_192 (nand_192_out, f, f);
  nand nand_193 (nand_193_out, b, b);
  nand nand_194 (nand_194_out, b, nand_169_out);
  nand nand_195 (nand_195_out, f, nand_170_out);
  nand nand_196 (nand_196_out, nand_171_out, nand_172_out);
  nand nand_197 (z, nand_173_out, nand_174_out);
  nand nand_198 (nand_198_out, nand_176_out, nand_177_out);
  nand nand_199 (nand_199_out, nand_178_out, nand_179_out);
  nand nand_200 (nand_200_out, c, g);
  nand nand_201 (nand_201_out, nand_180_out, nand_181_out);
  nand nand_202 (nand_202_out, b, f);
  nand nand_203 (nand_203_out, a, a);
  nand nand_204 (nand_204_out, e, e);
  nand nand_205 (nand_205_out, nand_182_out, nand_183_out);
  nand nand_206 (nand_206_out, a, nand_184_out);
  nand nand_207 (nand_207_out, e, nand_185_out);
  nand nand_208 (nand_208_out, nand_186_out, nand_187_out);
  nand nand_209 (nand_209_out, nand_188_out, nand_188_out);
  nand nand_210 (nand_210_out, nand_189_out, nand_189_out);
  nand nand_211 (nand_211_out, nand_190_out, nand_191_out);
  nand nand_212 (nand_212_out, b, nand_192_out);
  nand nand_213 (nand_213_out, f, nand_193_out);
  nand nand_214 (nand_214_out, nand_194_out, nand_195_out);
  nand nand_215 (nand_215_out, nand_196_out, nand_196_out);
  nand nand_216 (nand_216_out, c, g);
  nand nand_217 (nand_217_out, nand_198_out, nand_199_out);
  nand nand_218 (nand_218_out, nand_200_out, nand_200_out);
  nand nand_219 (nand_219_out, nand_201_out, nand_201_out);
  nand nand_220 (nand_220_out, nand_202_out, nand_202_out);
  nand nand_221 (nand_221_out, nand_203_out, nand_204_out);
  nand nand_222 (nand_222_out, nand_205_out, nand_205_out);
  nand nand_223 (nand_223_out, nand_206_out, nand_207_out);
  nand nand_224 (nand_224_out, nand_208_out, nand_208_out);
  nand nand_225 (nand_225_out, nand_209_out, nand_210_out);
  nand nand_226 (nand_226_out, nand_211_out, nand_211_out);
  nand nand_227 (nand_227_out, nand_212_out, nand_213_out);
  nand nand_228 (nand_228_out, nand_214_out, nand_214_out);
  nand nand_229 (nand_229_out, nand_215_out, nand_216_out);
  nand nand_230 (nand_230_out, nand_217_out, nand_217_out);
  nand nand_231 (nand_231_out, nand_218_out, nand_219_out);
  nand nand_232 (nand_232_out, nand_220_out, nand_221_out);
  nand nand_233 (nand_233_out, a, e);
  nand nand_234 (nand_234_out, nand_222_out, nand_223_out);
  nand nand_235 (nand_235_out, nand_224_out, nand_225_out);
  nand nand_236 (nand_236_out, nand_226_out, nand_227_out);
  nand nand_237 (nand_237_out, nand_228_out, nand_229_out);
  nand nand_238 (nand_238_out, nand_230_out, nand_231_out);
  nand nand_239 (nand_239_out, nand_232_out, nand_233_out);
  nand nand_240 (x, nand_234_out, nand_235_out);
  nand nand_241 (y, nand_236_out, nand_237_out);
  nand nand_242 (nand_242_out, nand_238_out, nand_238_out);
  nand nand_243 (nand_243_out, nand_239_out, nand_239_out);
  nand nand_244 (cout, nand_242_out, nand_243_out);
endmodule

module _4_bit_LCU_for_analysis_two_input_only (
  input  a,
  input  b,
  input  c,
  input  d,
  input  e,
  input  f,
  input  g,
  input  h,
  input  cin,
  output x,
  output y,
  output z,
  output u,
  output cout
);

  wire and_1_out, and_2_out, and_3_out, and_4_out, and_5_out, and_6_out, and_7_out, and_8_out, and_9_out,
       and_10_out, and_11_out, and_12_out, and_13_out, and_14_out, and_15_out, and_16_out, and_17_out,
       and_18_out, and_19_out, and_20_out, and_21_out, and_22_out, and_23_out, and_24_out, and_25_out,
       and_26_out, and_27_out, and_28_out, and_29_out, and_30_out, and_31_out, and_32_out, and_33_out,
       and_34_out, and_35_out, and_36_out, and_37_out, and_38_out, and_39_out, and_40_out, and_41_out,
       and_42_out, and_43_out, and_44_out, and_45_out, and_46_out, nand_1_out, nand_2_out, nand_3_out,
       nand_4_out, nand_5_out, nand_6_out, nand_7_out, nand_8_out, nand_9_out, nand_10_out, nand_11_out,
       nand_12_out, nand_13_out, nand_14_out, nand_15_out, nand_16_out, nand_17_out, nand_18_out,
       nand_19_out, nand_20_out, nand_21_out, nand_22_out, nand_23_out, nand_24_out, nand_25_out,
       nand_26_out, nand_27_out, nand_28_out, nand_31_out, nand_32_out, nand_33_out, nand_34_out, nor_1_out,
       nor_2_out, nor_3_out, not_1_out, not_2_out, not_3_out, not_4_out, not_5_out, not_6_out, not_7_out,
       not_8_out, not_9_out, not_10_out, not_11_out, not_12_out, not_13_out, not_14_out, not_15_out,
       not_16_out, not_17_out, not_18_out, not_19_out, not_20_out, not_21_out, or_1_out, or_2_out, or_3_out,
       or_4_out, or_5_out, or_6_out, or_7_out, or_8_out, or_9_out, or_10_out, or_11_out, or_12_out,
       or_13_out, or_14_out, or_15_out, or_16_out, or_17_out, or_18_out, or_19_out, or_20_out, or_21_out,
       or_22_out, or_23_out, or_24_out, or_25_out, or_26_out, or_27_out, or_28_out, or_29_out, or_30_out,
       or_31_out, or_32_out, or_33_out, or_34_out, or_35_out, or_36_out, or_37_out, or_38_out, or_39_out,
       or_40_out, or_41_out, or_42_out;

  or or_1 (or_1_out, d, h);
  or or_2 (or_2_out, c, g);
  or or_3 (or_3_out, b, f);
  or or_4 (or_4_out, c, g);
  or or_5 (or_5_out, b, f);
  or or_6 (or_6_out, d, h);
  or or_7 (or_7_out, c, g);
  or or_8 (or_8_out, b, f);
  or or_9 (or_9_out, c, g);
  or or_10 (or_10_out, b, f);
  or or_11 (or_11_out, d, h);
  or or_12 (or_12_out, d, h);
  or or_13 (or_13_out, d, h);
  not not_1 (not_1_out, g);
  not not_2 (not_2_out, c);
  not not_3 (not_3_out, g);
  not not_4 (not_4_out, c);
  not not_5 (not_5_out, h);
  not not_6 (not_6_out, d);
  not not_7 (not_7_out, h);
  not not_8 (not_8_out, d);
  or or_14 (or_14_out, d, h);
  and and_1 (and_1_out, cin, or_1_out);
  and and_2 (and_2_out, or_2_out, or_3_out);
  and and_3 (and_3_out, d, h);
  and and_4 (and_4_out, or_4_out, or_5_out);
  and and_5 (and_5_out, c, g);
  or or_15 (or_15_out, b, f);
  not not_9 (not_9_out, e);
  not not_10 (not_10_out, a);
  and and_6 (and_6_out, cin, or_6_out);
  and and_7 (and_7_out, or_7_out, or_8_out);
  and and_8 (and_8_out, d, h);
  and and_9 (and_9_out, or_9_out, or_10_out);
  and and_10 (and_10_out, c, g);
  or or_16 (or_16_out, b, f);
  and and_11 (and_11_out, cin, or_11_out);
  or or_17 (or_17_out, c, g);
  and and_12 (and_12_out, d, h);
  or or_18 (or_18_out, c, g);
  not not_11 (not_11_out, f);
  not not_12 (not_12_out, b);
  and and_13 (and_13_out, cin, or_12_out);
  or or_19 (or_19_out, c, g);
  and and_14 (and_14_out, d, h);
  or or_20 (or_20_out, c, g);
  and and_15 (and_15_out, cin, or_13_out);
  and and_16 (and_16_out, d, h);
  nand nand_1 (nand_1_out, c, not_1_out);
  nand nand_2 (nand_2_out, g, not_2_out);
  nand nand_3 (nand_3_out, c, not_3_out);
  nand nand_4 (nand_4_out, g, not_4_out);
  and and_17 (and_17_out, cin, or_21_out);
  or or_21 (or_21_out, d, h);
  and and_18 (and_18_out, d, h);
  nand nand_5 (nand_5_out, d, not_5_out);
  nand nand_6 (nand_6_out, h, not_6_out);
  nand nand_7 (nand_7_out, d, not_7_out);
  nand nand_8 (nand_8_out, h, not_8_out);
  and and_19 (and_19_out, cin, or_14_out);
  or or_22 (or_22_out, c, g);
  or or_23 (or_23_out, b, f);
  or or_24 (or_24_out, a, e);
  and and_20 (and_20_out, d, h);
  or or_25 (or_25_out, d, h);
  or or_26 (or_26_out, c, g);
  or or_27 (or_27_out, a, e);
  and and_21 (and_21_out, and_1_out, and_2_out);
  and and_22 (and_22_out, and_3_out, and_4_out);
  and and_23 (and_23_out, and_5_out, or_15_out);
  and and_24 (and_24_out, b, f);
  not not_13 (not_13_out, e);
  not not_14 (not_14_out, a);
  nand nand_9 (nand_9_out, a, not_9_out);
  nand nand_10 (nand_10_out, e, not_10_out);
  and and_25 (and_25_out, and_6_out, and_7_out);
  and and_26 (and_26_out, and_8_out, and_9_out);
  and and_27 (and_27_out, and_10_out, or_16_out);
  and and_28 (and_28_out, b, f);
  and and_29 (and_29_out, and_11_out, or_17_out);
  and and_30 (and_30_out, and_12_out, or_18_out);
  not not_15 (not_15_out, f);
  not not_16 (not_16_out, b);
  nand nand_11 (nand_11_out, b, not_11_out);
  nand nand_12 (nand_12_out, f, not_12_out);
  and and_31 (and_31_out, and_13_out, or_19_out);
  and and_32 (and_32_out, and_14_out, or_20_out);
  nor nor_1 (nor_1_out, and_15_out, and_16_out);
  nand nand_13 (nand_13_out, nand_1_out, nand_2_out);
  not not_17 (not_17_out, nand_14_out);
  nand nand_14 (nand_14_out, nand_3_out, nand_4_out);
  or or_28 (or_28_out, and_17_out, and_18_out);
  not not_18 (not_18_out, cin);
  nand nand_15 (nand_15_out, nand_5_out, nand_6_out);
  not not_19 (not_19_out, nand_16_out);
  nand nand_16 (nand_16_out, nand_7_out, nand_8_out);
  and and_33 (and_33_out, and_19_out, or_22_out);
  and and_34 (and_34_out, or_23_out, or_24_out);
  and and_35 (and_35_out, and_20_out, or_25_out);
  and and_36 (and_36_out, or_26_out, or_27_out);
  or or_29 (or_29_out, b, f);
  or or_30 (or_30_out, a, e);
  or or_31 (or_31_out, and_21_out, and_22_out);
  or or_32 (or_32_out, and_23_out, and_24_out);
  nand nand_17 (nand_17_out, a, not_13_out);
  nand nand_18 (nand_18_out, e, not_14_out);
  nand nand_19 (nand_19_out, nand_9_out, nand_10_out);
  or or_33 (or_33_out, and_25_out, and_26_out);
  or or_34 (or_34_out, and_27_out, and_28_out);
  or or_35 (or_35_out, and_29_out, and_30_out);
  and and_37 (and_37_out, c, g);
  nand nand_20 (nand_20_out, b, not_15_out);
  nand nand_21 (nand_21_out, f, not_16_out);
  nand nand_22 (nand_22_out, nand_11_out, nand_12_out);
  or or_36 (or_36_out, and_31_out, and_32_out);
  and and_38 (and_38_out, c, g);
  nand nand_23 (nand_23_out, nor_1_out, nand_13_out);
  nand nand_24 (nand_24_out, not_17_out, or_28_out);
  nand nand_25 (nand_25_out, not_18_out, nand_15_out);
  nand nand_26 (nand_26_out, not_19_out, cin);
  and and_39 (and_39_out, and_33_out, and_34_out);
  or or_37 (or_37_out, and_39_out, and_40_out);
  and and_40 (and_40_out, and_35_out, and_36_out);
  and and_41 (and_41_out, c, g);
  and and_42 (and_42_out, and_41_out, and_43_out);
  and and_43 (and_43_out, or_29_out, or_30_out);
  and and_44 (and_44_out, b, f);
  and and_45 (and_45_out, and_44_out, or_38_out);
  or or_38 (or_38_out, a, e);
  and and_46 (and_46_out, a, e);
  nor nor_2 (nor_2_out, or_31_out, or_32_out);
  nand nand_27 (nand_27_out, nand_17_out, nand_18_out);
  not not_20 (not_20_out, nand_19_out);
  or or_39 (or_39_out, or_33_out, or_34_out);
  nor nor_3 (nor_3_out, or_35_out, and_37_out);
  nand nand_28 (nand_28_out, nand_20_out, nand_21_out);
  not not_21 (not_21_out, nand_22_out);
  or or_40 (or_40_out, or_36_out, and_38_out);
  nand nand_29 (z, nand_23_out, nand_24_out);
  nand nand_30 (u, nand_25_out, nand_26_out);
  or or_41 (or_41_out, or_37_out, and_42_out);
  or or_42 (or_42_out, and_45_out, and_46_out);
  nand nand_31 (nand_31_out, nor_2_out, nand_27_out);
  nand nand_32 (nand_32_out, not_20_out, or_39_out);
  nand nand_33 (nand_33_out, nor_3_out, nand_28_out);
  nand nand_34 (nand_34_out, not_21_out, or_40_out);
  or or_43 (cout, or_41_out, or_42_out);
  nand nand_35 (x, nand_31_out, nand_32_out);
  nand nand_36 (y, nand_33_out, nand_34_out);
endmodule

module _4th_LCU (
  input  g1,
  input  g2,
  input  g3,
  input  g4,
  input  p1,
  input  p2,
  input  p3,
  input  p4,
  input  cin,
  output cout
);

  wire and_1_out, and_2_out, and_3_out, and_4_out;

  and and_1 (and_1_out, cin, p1, p2, p3, p4);
  and and_2 (and_2_out, g1, p1, p2, p4);
  and and_3 (and_3_out, g3, p4);
  and and_4 (and_4_out, g2, p3, p4);
  or or_1 (cout, and_1_out, and_2_out, and_4_out, and_3_out, g4);
endmodule

module _4th_LCU_2 (
  input  g1,
  input  g2,
  input  g3,
  input  g4,
  input  p1,
  input  p2,
  input  p3,
  input  p4,
  input  cin,
  output cout
);

  wire nand_1_out, nand_2_out, nand_3_out, nand_4_out, nand_5_out, nand_6_out, nor_1_out, nor_2_out,
       nor_3_out, not_1_out, not_2_out, not_3_out;

  nand nand_1 (nand_1_out, p2, p3, p4);
  not not_1 (not_1_out, p1);
  nor nor_1 (nor_1_out, not_1_out, nand_1_out);
  nand nand_2 (nand_2_out, cin, nor_1_out);
  not not_2 (not_2_out, g1);
  nand nand_3 (nand_3_out, p1, p2, p4);
  nor nor_2 (nor_2_out, not_2_out, nand_3_out);
  nand nand_4 (nand_4_out, g2, p3, p4);
  nand nand_5 (nand_5_out, g3, p4);
  not not_3 (not_3_out, g4);
  nand nand_6 (nand_6_out, nand_4_out, nand_5_out, not_3_out);
  nor nor_3 (nor_3_out, nor_2_out, nand_6_out);
  nand nand_7 (cout, nand_2_out, nor_3_out);
endmodule

module AOI21 (
  input  X,
  input  Y,
  input  C,
  output out_4
);

  wire transistor_1_out, transistor_6_out;

  Transistor transistor_1 (.in(1'b1), .out(transistor_1_out), .gate(C));
  Transistor transistor_2 (.in(1'b1), .out(transistor_1_out), .gate(Y));
  Transistor transistor_3 (.in(transistor_1_out), .out(out_4), .gate(X));
  Transistor #(.\type ("n"), .gate("br")) transistor_4 (.in(1'b0), .out(out_4), .gate(X));
  Transistor #(.\type ("n"), .gate("br")) transistor_5 (.in(transistor_6_out), .out(out_4), .gate(Y));
  Transistor #(.\type ("n"), .gate("br")) transistor_6 (.in(1'b0), .out(transistor_6_out), .gate(C));
endmodule

module _4th_LCU_3 (
  input  g1,
  input  g2,
  input  g3,
  input  g4,
  input  p1,
  input  p2,
  input  p3,
  input  p4,
  input  cin,
  output cout
);

  wire aoi21_1_out_4, nand_1_out, nand_2_out, nand_3_out, nand_4_out, nor_1_out, nor_2_out, nor_3_out,
       nor_4_out, nor_5_out, nor_6_out, not_1_out, not_2_out, not_3_out, not_4_out, not_5_out, not_6_out,
       not_7_out;

  not not_1 (not_1_out, p3);
  not not_2 (not_2_out, p4);
  not not_3 (not_3_out, g2);
  nand nand_1 (nand_1_out, not_1_out, not_2_out, not_3_out);
  not not_4 (not_4_out, g1);
  nand nand_2 (nand_2_out, not_1_out, not_2_out, not_4_out);
  nor nor_1 (nor_1_out, p4, g3);
  nand nand_3 (nand_3_out, nand_1_out, nor_6_out);
  nor nor_2 (nor_2_out, p2, nand_2_out);
  nor nor_3 (nor_3_out, nor_2_out, nand_3_out);
  not not_5 (not_5_out, p1);
  not not_6 (not_6_out, p2);
  nor nor_4 (nor_4_out, not_6_out, not_5_out);
  nand nand_4 (nand_4_out, p3, nor_4_out);
  nor nor_5 (nor_5_out, not_2_out, nand_4_out);
  not not_7 (not_7_out, g4);
  AOI21 aoi21_1 (.X(nor_5_out), .Y(nor_3_out), .C(cin), .out_4(aoi21_1_out_4));
  nor nor_6 (nor_6_out, nor_1_out, not_7_out);
  not not_8 (cout, aoi21_1_out_4);
endmodule
