// Logisim project sub-add circ.circ as structural Verilog: 2 circuits, main circuit sub/add
module sub_add (
  input  sub,
  input  cin,
  input  select,
  input  [15:0] a,
  input  [15:0] b,
  output cout,
  output [15:0] result,
  output overflow
);

  wire and_1_out, and_2_out, logic_mux2_1_p4, not_1_out, not_2_out, not_3_out;
  wire [15:0] xor_1_out;

  // logic_mux2 logic_mux2_1: pin names not known; wires that end beside it: sub, cin, select, logic_mux2_1_p4
  xor xor_1 (xor_1_out[0], b[0], sub);
  xor xor_2 (xor_1_out[1], b[1], sub);
  xor xor_3 (xor_1_out[2], b[2], sub);
  xor xor_4 (xor_1_out[3], b[3], sub);
  xor xor_5 (xor_1_out[4], b[4], sub);
  xor xor_6 (xor_1_out[5], b[5], sub);
  xor xor_7 (xor_1_out[6], b[6], sub);
  xor xor_8 (xor_1_out[7], b[7], sub);
  xor xor_9 (xor_1_out[8], b[8], sub);
  xor xor_10 (xor_1_out[9], b[9], sub);
  xor xor_11 (xor_1_out[10], b[10], sub);
  xor xor_12 (xor_1_out[11], b[11], sub);
  xor xor_13 (xor_1_out[12], b[12], sub);
  xor xor_14 (xor_1_out[13], b[13], sub);
  xor xor_15 (xor_1_out[14], b[14], sub);
  xor xor_16 (xor_1_out[15], b[15], sub);
  // _16_bit_Carry_Select_Adder 16_bit_carry_select_adder_1: pin names not known; wires that end beside it: a, xor_1_out, logic_mux2_1_p4, cout, result
  not not_1 (not_1_out, a[15]);
  not not_2 (not_2_out, xor_1_out[15]);
  and and_1 (and_1_out, not_1_out, not_2_out, result[15]);
  and and_2 (and_2_out, a[15], xor_1_out[15], not_3_out);
  not not_3 (not_3_out, result[15]);
  or or_1 (overflow, and_1_out, and_2_out);
endmodule

module control (
  input  in_1,
  input  sub_add,
  input  [15:0] a,
  input  [15:0] b,
  input  reset,
  output [15:0] out_6
);

  wire clock_1_out, register_3_q;
  wire [15:0] register_1_q, register_2_q, sub_add_1_result;

  Clock clock_1 (.out(clock_1_out));
  Register #(.width(16)) register_1 (.D(a), .en(1'b1), .Q(register_1_q), .clk(clock_1_out), .clr(reset));
  Register #(.width(16)) register_2 (.D(b), .en(1'b1), .Q(register_2_q), .clk(clock_1_out), .clr(reset));
  Register #(.width(1)) register_3 (.D(sub_add), .en(1'b1), .Q(register_3_q), .clk(clock_1_out));  // open: clr
  sub_add sub_add_1 (
    .cin(in_1), .sub(register_3_q), .a(register_1_q), .b(register_2_q), .result(sub_add_1_result));  // open: cout, overflow, select
  Register #(.width(16)) register_4 (.D(sub_add_1_result), .en(1'b1), .Q(out_6), .clk(clock_1_out), .clr(reset));
endmodule
